# Fritzing sketch SERVO_POT (saved by Fritzing 0.9.2b)
breadboards: 1

parts:
  J1 = Basic Servo
  Componente1 = Arduino Uno (Rev3)
  R1 = Rotary Potentiometer (Small) [maximum_resistance=100kΩ package=THT]
  U1 = LCD-16X2 [package=lcd-16x2_noholes]  # not connected

nets:
  GND: J1.gnd, Componente1.GND, R1.leg1
  VCC: J1.vcc, Componente1.5V, R1.leg2
  N1: J1.pulse, Componente1.D6_PWM
  N2: Componente1.A0, R1.wiper

notes:
  Collegamento LCD I2C
  VCC >> 5v
  GND >> GND
  SCL >> Arduino Pin A5
  SDA >> Arduino Pin A4
