# Fritzing sketch Trasmettitore-Ricevitore (saved by Fritzing 0.9.2b)
breadboards: 1

parts:
  Componente1 = Arduino Uno (Rev3)
  S1 = Pushbutton [package=THT]
  Componente2 = Arduino Uno (Rev3)
  NRF24L2 = NRF24L01
  NRF24L3 = NRF24L01
  LED1 = LED - 5mm [color="Red (633nm)" package="5 mm [THT]"]
  R1 = Resistor [tolerance=±5% resistance=220 package=THT]

nets:
  N1: Componente1.D9_PWM, NRF24L2.CE
  N2: Componente1.D10_PWM/SS, NRF24L2.CSN
  N3: Componente1.D11_PWM/MOSI, NRF24L2.MOSI
  N4: Componente1.D12/MISO, NRF24L2.MISO
  N5: Componente1.D13/SCK, NRF24L2.SCK
  N6: Componente1.D7, S1.leg1
  3V3: Componente1.3V3, NRF24L2.VCC
  GND: Componente1.GND, S1.leg0, NRF24L2.GND
  N7: Componente2.D9_PWM, NRF24L3.CE
  N8: Componente2.D10_PWM/SS, NRF24L3.CSN
  N9: Componente2.D11_PWM/MOSI, NRF24L3.MOSI
  N10: Componente2.D12/MISO, NRF24L3.MISO
  N11: Componente2.D13/SCK, NRF24L3.SCK
  N12: Componente2.D7, R1.Pin_0
  3V3_2: Componente2.3V3, NRF24L3.VCC
  GND_2: Componente2.GND, NRF24L3.GND, LED1.cathode
  N13: LED1.anode, R1.Pin_1

custom parts:
  NRF24L01: NRF24L01 module
