# Fritzing sketch BME280 (saved by Fritzing 0.9.3b)
breadboards: 1

parts:
  Componente1 = Arduino Uno (Rev3)
  U1 = LCD-16X2 [package=lcd-16x2]  # not connected
  S1 = Momentary Switch [package=ksa_sealed_tac_switch]

nets:
  N1: Componente1.GND, S1.1
  N2: Componente1.D3_PWM, S1.3
