# Fritzing sketch WEB_SERVER (saved by Fritzing 0.9.3b)
breadboards: 1

parts:
  Componente1 = Arduino Uno (Rev3)  # not connected
  Componente2 = Arduino Ethernet Shield (Rev3)
  LED1 = LED - 5mm [color="Red (633nm)" package="5 mm [THT]"]
  R1 = Resistor [tolerance=±5% resistance=220 package=THT]
  U1 = POT [package=alps_pot]

nets:
  N1: Componente2.A0, U1.S
  N2: Componente2.PWM_D5, R1.Pin_1
  N3: Componente2.5V, U1.E
  N4: Componente2.GND, LED1.cathode, U1.A
  N5: LED1.anode, R1.Pin_0
